# Fritzing sketch Sketch (saved by Fritzing 0.9.3b)

parts:
  Part1 = Arduino Uno (Rev3)
  IR2 = TSOP312.., 314.. [package=THT]

nets:
  N1: Part1.D11_PWM/MOSI, IR2.Data
  5V: Part1.5V, IR2.Vcc
  GND: Part1.GND, IR2.GND

custom parts:
  TSOP312.., 314..: The TSOP312.., TSOP314.. series are miniaturized receivers for infrared remote control systems. A PIN diode and a preamplifier are assembled on a lead frame, the epoxy package acts as an IR filter. The demodulated output signal can be directly decoded by a microprocessor. The TSOP312.. is compatible with all common IR remote control data formats. The TSOP314.. is optimized to suppress almost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

// code stored in the sketch: ControleRemotoIR.ino
/*
 * IRremote: IRrecvDemo - demonstrates receiving IR codes with IRrecv
 * An IR detector/demodulator must be connected to the input RECV_PIN.
 * Version 0.1 July, 2009
 * Copyright 2009 Ken Shirriff
 * http://arcfn.com
 */

#include <IRremote.h>

int RECV_PIN = 11;
byte byteRead = 0;

String leStringSerial(); //prototipagem do método

IRrecv irrecv(RECV_PIN);

decode_results results;

void setup()
{
  Serial.begin(9600);
  Serial.println("CONTROLE");
  irrecv.enableIRIn(); // Start the receiver
}

void loop() {
  if (irrecv.decode(&results)) {
    Serial.println(results.value, HEX);
    irrecv.resume(); // Receive the next value
  }
  delay(100);
  if (leStringSerial() == "QMEH")
  {
    Serial.println("CONTROLE");
  }
}

String leStringSerial(){
  String conteudo = "";
  char caractere;
  
  // Enquanto receber algo pela serial
  while(Serial.available() > 0) {
    // Lê byte da serial
    caractere = Serial.read();
    // Ignora caractere de quebra de linha
    if (caractere != '\n'){
      // Concatena valores
      conteudo.concat(caractere);
    }
    // Aguarda buffer serial ler próximo caractere
    delay(10);
  }    
  return conteudo;
}
